# Fritzing sketch Cycluino (saved by Fritzing 0.9.3b)

parts:
  Part1 = Arduino Mega 2560 (Rev3)
  Part5 = KY-003 Hall Magnetic Sensor Module [package="Breakout board"]
  BMP280_Breakout1 = BMP280 Breakout Board [part_number=BMP280]
  GY-1 = GY-273 [part_number=GY-273]
  ZS-042_RTC1 = ZS-042 RTC Module
  3LED_Rotary_Encoder_DIP1 = 3 LED & RE & SW DIP [package=DIP]
  Part6 = Bluetooth HC-05 Macho
  Part7 = TFT 1.8 inch 160x128 w microSD [part_number=358]
  U1 = LIPO-1000mAh [package=lipo-1000]
  Part8 = USB LiPoly Charger
  MP1584EN_Board1 = MP1584EN Power Regulator Board [part_number=MP1584EN]
  Part9 = KY-003 Hall Magnetic Sensor Module [package="Breakout board"]
  R1 = Resistor [tolerance=±5% resistance=47k package=THT]
  D1 = Diode [package=diode-1n4001]
  R2 = Resistor [tolerance=±5% resistance=10k package=THT]

nets:
  N1: Part1.A0, D1.C
  N2: Part1.D21/SCL, BMP280_Breakout1.SCL, GY-1.SCL, ZS-042_RTC1.SCL
  N3: Part1.D20/SDA, BMP280_Breakout1.SDA, GY-1.SDA, ZS-042_RTC1.SDA
  N4: Part1.D19/RX1, Part5.S
  N5: Part1.D15/RX3, Part6.TXD
  N6: Part1.D14/TX3, Part6.RXD
  GND: Part1.GND, Part5.-, BMP280_Breakout1.GND, GY-1.GND, ZS-042_RTC1.GND, 3LED_Rotary_Encoder_DIP1.GND, Part6.GND, Part7.GND, MP1584EN_Board1.OUT_-, Part9.-
  N7: Part1.D8_PWM, Part7.CARDCS
  VCC: Part1.5V, Part5.Vin, BMP280_Breakout1.VCC, GY-1.VCC, ZS-042_RTC1.VCC, 3LED_Rotary_Encoder_DIP1.VCC, Part6.VCC, Part7.+5V, Part9.Vin, R1.Pin_0
  N8: Part1.VIN, MP1584EN_Board1.OUT_+
  N9: Part1.D2_PWM, Part9.S
  N10: Part1.D6_PWM, Part7.RESET
  N11: Part1.D7_PWM, Part7.TFTDC
  N12: Part1.D26, 3LED_Rotary_Encoder_DIP1.ENC_B
  N13: Part1.D28, 3LED_Rotary_Encoder_DIP1.ENC_A
  N14: Part1.D30, 3LED_Rotary_Encoder_DIP1.SWITCH
  N15: Part1.D35, Part6.State
  N16: Part1.D37, Part6.Key
  N17: Part1.D50, Part7.MISO
  N18: Part1.D51, Part7.MOSI
  N19: Part1.D52, Part7.SCLK
  N20: Part1.D53, Part7.TFTCS
  N21: Part7.LITE, R1.Pin_1
  N22: U1.+, Part8.VBAT, MP1584EN_Board1.IN_+, R2.Pin_0
  N23: U1.-, Part8.GND, MP1584EN_Board1.IN_-
  N24: D1.A, R2.Pin_1

custom parts:
  KY-003 Hall Magnetic Sensor Module: KEYES KY-003 Arduino Hall Magnetic Sensor Module is a switch that will turn on/off in the presence of a magnetic field.
  BMP280 Breakout Board: This is a breakout board for the Bosch Sensortec BMP280, "an absolute barometric pressure sensor especially designed for mobile applications." The operation range is 300 to 1100 hPa. Supply voltage is 1.2 to 3.6V. Operating temperature range is -40 to +85 °C.
  GY-273: GY-273 - Electronic compass module - 3 Axis Magnetic Field Sensor HMC5883L
  3 LED & RE & SW DIP: RGB color LED and Rotary Encoder with Switch on PCB board. LED and SW are anode common.
  TFT 1.8 inch 160x128 w microSD: This lovely little display breakout is the best way to add a small, colorful and bright display to any project. Since the display uses 4-wire SPI to communicate and has its own pixel-addressable frame buffer, it can be used with every kind of microcontroller. Even a very small one with low memory and few pins available! The 1.8" display has 128x160 color pixels.
  MP1584EN Power Regulator Board: The MP1584EN is a high frequency step-down switching regulator. The input voltage range is 4.5V to 28V. The output voltage is set by the board's potentiometer.
